# Fritzing sketch Finished circuit drawing (saved by Fritzing 0.9.3b)
breadboards: 1

parts:
  Part1 = Arduino Nano (Rev3.0)
  C1 = Electrolytic Capacitor [capacitance=1µF package="100 mil [THT, electrolytic]"]
  J1 = Piezo Speaker
  LED1 = LED - 5mm [color="Red (633nm)" package="5 mm [THT]"]
  Part2 = Triple Axis Accelerometer Breakout - ADXL335
  R1 = Resistor [tolerance=±5% resistance=220 package=THT]  # not connected
  R2 = Resistor [tolerance=±5% resistance=220 package=THT]
  J2 = Basic Servo
  hc-sr1 = hc-sr04

nets:
  GND: Part1.GND, C1.-, LED1.anode, Part2.XOUT, J2.gnd
  N1: Part1.D2, hc-sr1.Echo
  N2: Part1.D3, R2.Pin_1, J2.pulse
  N3: Part1.D5, J1.pin2, hc-sr1.Trig
  VCC: Part1.5V, C1.+, J1.pin1, Part2.YOUT, J2.vcc, hc-sr1.VCC
  N4: Part1.A5, Part2.GND
  N5: Part1.A4, Part2.VCC
